// Digital circuit partial_processor.dig as structural Verilog
module partial_processor (
  input  clk,
  output [31:0] R
);

  wire a_mul, ALUsrcB, C, CLK_t, CLR, done, i_dp, N, RFW, V, Z;
  wire [1:0] EXTop;
  wire [2:0] ALUOp;
  wire [3:0] cond;
  wire [23:0] b_offset;
  wire [27:24] iw;
  wire [31:0] add_2_s, extension_unit_1_extimm, multiplexer_1_out, PC_p1, PC_p5, r0, r1, r2, r3, r4, r5, r6,
       r7, r8, r9, r10, r11, r12, r13, r14, r15, register_file_1_rd0, register_file_1_rd1;

  and and_1 (CLK_t, clk, ~done);  // And
  // register PC: pin names not known; wires that end beside it: PC_p1, CLK_t, 1'b1, CLR, PC_p5
  // Probe on {cond, iw[27:26], i_dp, iw[24], b_offset[23:22], a_mul, b_offset[20:0]}
  DipSwitch #(.dipDefault("true")) dipswitch_1 (.out(CLR));
  Add #(.Bits(32)) add_1 (.a(PC_p5), .b(32'h4), .c_i(1'b0), .s(PC_p1));  // open: c_o
  decoder decoder_1 (
    .iw({cond, iw[27:26], i_dp, iw[24], b_offset[23:22], a_mul, b_offset[20:0]}), .RFW(RFW), .EXTop(EXTop),
    .ALUsrcB(ALUsrcB), .ALUop(ALUOp));
  ROM #(.AddrBits(5), .Bits(32)) rom_1 (
    .A(PC_p5[6:2]), .sel(1'b1), .D({cond, iw[27:26], i_dp, iw[24], b_offset[23:22], a_mul, b_offset[20:0]}));
  Add #(.Bits(32)) add_2 (.a(PC_p1), .b(32'h4), .c_i(1'b0), .s(add_2_s));  // open: c_o
  // Probe on r0
  // Probe on r2
  // Probe on r4
  // Probe on r6
  // Probe on cond
  // Probe on cond
  // Probe on cond
  // Probe on cond
  register_file register_file_1 (
    .ReadReg0(b_offset[19:16]), .ReadReg1(b_offset[3:0]), .WriteReg(b_offset[15:12]), .WriteData(R),
    .WriteEn(RFW), .PC(add_2_s), .CLK(CLK_t), .CLR(CLR), .RD0(register_file_1_rd0),
    .RD1(register_file_1_rd1), .r0(r0), .r1(r1), .r2(r2), .r3(r3), .r4(r4), .r5(r5), .r6(r6), .r7(r7),
    .r8(r8), .r9(r9), .r10(r10), .r11(r11), .r12(r12), .r13(r13), .r14(r14), .r15(r15));
  // Probe on r1
  // Probe on r3
  // Probe on r5
  // Probe on r7
  // Probe on iw[27:26]
  // Probe on {iw[27:26], i_dp, iw[24], b_offset[23]}
  // Probe on iw[27:26]
  // Probe on {iw[27:26], i_dp}
  // Probe on i_dp
  // Probe on a_mul
  // Probe on i_dp
  // Probe on iw[24]
  // Probe on r8
  // Probe on r10
  // Probe on r12
  // Probe on r14
  // Probe on {iw[24], b_offset[23:22], a_mul}
  // Probe on b_offset[20]
  // Probe on iw[24]
  // Probe on {b_offset[23:22], a_mul, b_offset[20:0]}
  Multiplexer #(.Bits(32)) multiplexer_1 (
    .sel(ALUsrcB), .in_0(register_file_1_rd1), .in_1(extension_unit_1_extimm), .out(multiplexer_1_out));
  extension_unit extension_unit_1 (
    .iw({cond, iw[27:26], i_dp, iw[24], b_offset[23:22], a_mul, b_offset[20:0]}), .EXTop(EXTop),
    .extimm(extension_unit_1_extimm));
  // Probe on r9
  // Probe on r11
  // Probe on r13
  // Probe on r15
  // Probe on b_offset[20]
  // Probe on b_offset[19:16]
  // Probe on b_offset[23]
  alu alu_1 (
    .ALUOp(ALUOp), .A(register_file_1_rd0), .B(multiplexer_1_out), .R(R), .N(N), .Z(Z), .C(C), .V(V));  // open: NZCV
  // Probe on b_offset[19:16]
  // Probe on b_offset[15:12]
  // Probe on b_offset[22]
  // Probe on N
  // Probe on Z
  // Probe on C
  // Probe on V
  // Probe on b_offset[15:12]
  // Probe on b_offset[11:8]
  // Probe on a_mul
  Comparator #(.Bits(32)) comparator_1 (
    .a({cond, iw[27:26], i_dp, iw[24], b_offset[23:22], a_mul, b_offset[20:0]}), .b(32'he2800000), .eq(done));  // open: gt, lt
  // Probe on b_offset[3:0]
  // Probe on b_offset[7:0]
  // Probe on b_offset[7:4]
  // Probe on b_offset[20]
  // Probe on b_offset[3:0]
  // Probe on b_offset[19:16]
  LED led_1 (.in(done));
  // Probe on b_offset[15:12]
  // Probe on b_offset[3:0]
  // Probe on b_offset[11:0]

  // Other names for the same wires on the sheet: imm[7:0] = b_offset[7:0]; immoff[11:0] = b_offset[11:0];
  //   iw (some bits) = {cond, i_dp, b_offset[23:22], a_mul, b_offset[20:0]}; rm[3:0] = b_offset[3:0];
  //   rm_mul[3:0] = b_offset[3:0]; opmul4[3:0] = b_offset[7:4]; rs_mul[3:0] = b_offset[11:8];
  //   rd[3:0] = b_offset[15:12]; rn_mul[3:0] = b_offset[15:12]; rd_mul[3:0] = b_offset[19:16];
  //   rn[3:0] = b_offset[19:16]; l_sdt = b_offset[20]; s_dp = b_offset[20]; s_mul = b_offset[20];
  //   b_offset[21] = a_mul; opc[3:0] = {iw[24], b_offset[23:22], a_mul}; w_sdt = a_mul; b_sdt = b_offset[22];
  //   opmul6[4:0] = {iw[27:26], i_dp, iw[24], b_offset[23]}; u_sdt = b_offset[23]; l_b = iw[24]; p_sdt = iw[24];
  //   i_sdt = i_dp; opb3[2:0] = {iw[27:26], i_dp}; op2[1:0] = iw[27:26]; opmul2[1:0] = iw[27:26]

  // Notes on the sheet:
  //   contents of rom_1 (hex, n*v repeats v):
  //   e3a00001,e3a01002,e0802001,e2800000
  //   DP
  //   MUL
  //   SDT
  //   B
  //   lr
  //   sp
  //   pc
endmodule
