// Digital circuit alu.dig as structural Verilog
module alu (
  input  [2:0] ALUOp,
  input  [31:0] A,
  input  [31:0] B,
  output [31:0] R,
  output N,
  output Z,
  output C,
  output V,
  output [3:0] NZCV
);

  wire and_1_out, and_2_out, and_3_out, and_4_out, and_6_out, and_7_out, comparator_2_eq, comparator_3_eq,
       comparator_4_eq, or_1_out, or_2_out, sub_1_c_o;
  wire [31:0] add_1_s, barrelshifter_1_out, barrelshifter_2_out, sub_1_s;
  wire [63:0] mul_1_mul;

  Add #(.Bits(32)) add_1 (.a(A), .b(B), .c_i(1'b0), .s(add_1_s));  // open: c_o
  Sub #(.Bits(32)) sub_1 (.a(A), .b(B), .c_i(1'b0), .s(sub_1_s), .c_o(sub_1_c_o));
  Mul #(.Bits(32)) mul_1 (.a(A), .b(B), .mul(mul_1_mul));
  BarrelShifter #(.Bits(32)) barrelshifter_1 (.in(A), .shift(B[5:0]), .out(barrelshifter_1_out));
  BarrelShifter #(.Bits(32), .direction("right")) barrelshifter_2 (.in(A), .shift(B[5:0]), .out(barrelshifter_2_out));
  Multiplexer #(.Selector_Bits(3), .Bits(32)) multiplexer_1 (
    .sel(ALUOp), .in_0(add_1_s), .in_1(sub_1_s), .in_2(mul_1_mul[31:0]), .in_3(B),
    .in_4(barrelshifter_1_out), .in_5(barrelshifter_2_out), .in_6({32{1'b0}}), .in_7({32{1'b0}}),
    .out({N, R[30:0]}));
  Comparator #(.Bits(32)) comparator_1 (.a({N, R[30:0]}), .b({32{1'b0}}), .eq(NZCV[1]));  // open: gt, lt
  and and_1 (and_1_out, ~A[31], B[31], N);  // And
  and and_2 (and_2_out, A[31], ~B[31], N);  // And
  and and_3 (and_3_out, A[31], B[31], N);
  and and_4 (and_4_out, ~A[31], ~B[31], N);  // And
  or or_1 (or_1_out, and_1_out, and_2_out);
  or or_2 (or_2_out, and_3_out, and_4_out);
  Comparator #(.Bits(3)) comparator_2 (.a(ALUOp), .b(3'b001), .eq(comparator_2_eq));  // open: gt, lt
  Comparator #(.Bits(3)) comparator_3 (.a(3'b001), .b(ALUOp), .eq(comparator_3_eq));  // open: gt, lt
  Comparator #(.Bits(3)) comparator_4 (.a(3'b000), .b(ALUOp), .eq(comparator_4_eq));  // open: gt, lt
  and and_5 (C, sub_1_c_o, comparator_2_eq);
  and and_6 (and_6_out, or_1_out, comparator_3_eq);
  and and_7 (and_7_out, ~comparator_4_eq, or_2_out);  // And
  or or_3 (NZCV[3], and_6_out, and_7_out);

  assign {NZCV[2], NZCV[0]} = {C, N};
  assign R[31] = N;
  assign V = NZCV[3];
  assign Z = NZCV[1];

  // Notes on the sheet:
  //   good
endmodule
