// Digital circuit decoder.dig as structural Verilog
module decoder (
  input  [31:0] iw,
  output RFW,
  output [1:0] EXTop,
  output ALUsrcB,
  output [2:0] ALUop,
  output [1:0] PCsel,
  output [1:0] RR0sel,
  output RR1sel,
  output WRsel,
  output WDsel
);

  wire add_i_eq, add_r_eq, b_eq, bl_eq, bx_eq, mov_i_eq, mov_r_eq;
  wire [1:0] multiplexer_1_out;
  wire [2:0] priorityencoder_1_num;

  // Probe on iw[27:20]
  // Probe on iw[27:24]
  // Probe on iw[27:4]
  Comparator #(.Bits(8)) add_r (.a(iw[27:20]), .b(8'h8), .eq(add_r_eq));  // open: gt, lt
  Comparator #(.Bits(8)) add_i (.a(iw[27:20]), .b(8'h28), .eq(add_i_eq));  // open: gt, lt
  Comparator #(.Bits(8)) mov_r (.a(iw[27:20]), .b(8'h1a), .eq(mov_r_eq));  // open: gt, lt
  Comparator #(.Bits(8)) mov_i (.a(iw[27:20]), .b(8'h3a), .eq(mov_i_eq));  // open: gt, lt
  Comparator #(.Bits(4)) b (.a(iw[27:24]), .b(4'b1010), .eq(b_eq));  // open: gt, lt
  Comparator #(.Bits(4)) bl (.a(iw[27:24]), .b(4'b1011), .eq(bl_eq));  // open: gt, lt
  Comparator #(.Bits(24)) bx (.a(iw[27:4]), .b(24'h12fff1), .eq(bx_eq));  // open: gt, lt
  PriorityEncoder #(.Selector_Bits(3)) priorityencoder_1 (
    .in0(add_r_eq), .in1(add_i_eq), .in2(mov_r_eq), .in3(mov_i_eq), .in4(b_eq), .in5(bl_eq), .in6(bx_eq),
    .in7(1'b0), .num(priorityencoder_1_num));  // open: any
  Multiplexer #(.Selector_Bits(3), .Bits(16)) multiplexer_1 (
    .sel(priorityencoder_1_num), .in_0(16'h8000), .in_1(16'h9000), .in_2(16'h8600), .in_3(16'h9600),
    .in_4(16'h50a0), .in_5(16'hd0ac), .in_6(16'h100), .in_7({16{1'b0}}),
    .out({RFW, EXTop, ALUsrcB, ALUop, PCsel, RR0sel, RR1sel, WRsel, WDsel, multiplexer_1_out}));
  // Probe on {RFW, EXTop, ALUsrcB, ALUop, PCsel, RR0sel, RR1sel, WRsel, WDsel, multiplexer_1_out}
  // Probe on RFW
  // Probe on EXTop
  // Probe on ALUsrcB
  // Probe on ALUop
  // Probe on PCsel
  // Probe on RR0sel
  // Probe on RR1sel
  // Probe on WRsel
  // Probe on WDsel

  // Other names for the same wires on the sheet: bits27_4[23:0] = iw[27:4]; bits27_20[7:0] = iw[27:20];
  //   bits27_24[3:0] = iw[27:24]
endmodule
