// Digital circuit lab08part1.dig as structural Verilog
module lab08part1 (
  input  Ain,
  input  Bin
);

  wire and_1_out, not_1_out, or_1_out, xor_1_out;

  not not_1 (not_1_out, Ain);
  and and_1 (and_1_out, Ain, Bin);
  or or_1 (or_1_out, Ain, Bin);
  xor xor_1 (xor_1_out, Ain, Bin);
  LED led_1 (.in(not_1_out));
  LED led_2 (.in(and_1_out));
  LED led_3 (.in(or_1_out));
  LED led_4 (.in(xor_1_out));

  // Notes on the sheet:
  //   Part 1: LEDs
  //   Not
  //   And
  //   Or
  //   Xor
endmodule
