// Digital circuit lab08part2.dig as structural Verilog
module lab08part2 (
  input  Ain,
  input  Bin,
  input  Cin,
  output out_4,
  output out_5
);

  wire and_1_out, and_2_out, and_3_out, and_4_out, and_5_out, and_6_out, and_7_out, and_8_out, or_1_out,
       or_2_out, or_3_out, or_4_out;

  and and_1 (and_1_out, ~Ain, ~Bin, Cin);  // And
  and and_2 (and_2_out, ~Ain, Bin, ~Cin);  // And
  and and_3 (and_3_out, Ain, ~Bin, ~Cin);  // And
  and and_4 (and_4_out, Ain, Bin, Cin);
  and and_5 (and_5_out, ~Ain, Bin, Cin);  // And
  and and_6 (and_6_out, Ain, ~Bin, Cin);  // And
  and and_7 (and_7_out, Ain, Bin, ~Cin);  // And
  and and_8 (and_8_out, Ain, Bin, Cin);
  or or_1 (or_1_out, and_1_out, and_2_out);
  or or_2 (or_2_out, and_3_out, and_4_out);
  or or_3 (or_3_out, and_5_out, and_6_out);
  or or_4 (or_4_out, and_7_out, and_8_out);
  or or_5 (out_4, or_1_out, or_2_out);
  or or_6 (out_5, or_3_out, or_4_out);

  // Notes on the sheet:
  //   Part 2: 1-bit full adder
  //   Sum Circuit
  //   Cout Circuit
  //   Sout
  //   Cout
endmodule
