// Digital circuit lab08part3.dig as structural Verilog
module lab08part3 (
  input  A1in,
  input  A0in,
  input  B1in,
  input  B0in,
  output out_5,
  output out_6
);

  wire and_1_out, and_2_out, and_3_out, and_4_out, and_5_out, and_6_out, and_7_out, and_8_out, and_9_out,
       and_10_out, and_11_out, and_12_out, and_13_out, and_14_out, and_15_out, and_16_out, and_17_out,
       and_18_out, and_19_out, and_20_out, and_21_out, and_22_out, or_1_out, or_2_out, or_3_out, or_4_out,
       or_5_out, or_6_out;

  and and_1 (and_1_out, ~A1in, ~A0in, B1in, ~B0in);  // And
  and and_2 (and_2_out, ~A1in, ~A0in, B1in, B0in);  // And
  and and_3 (and_3_out, ~A1in, A0in, B1in, ~B0in);  // And
  and and_4 (and_4_out, ~A1in, A0in, B1in, B0in);  // And
  and and_5 (and_5_out, A1in, ~A0in, ~B1in, ~B0in);  // And
  and and_6 (and_6_out, A1in, ~A0in, ~B1in, B0in);  // And
  and and_7 (and_7_out, A1in, ~A0in, B1in, ~B0in);  // And
  and and_8 (and_8_out, A1in, ~A0in, B1in, B0in);  // And
  and and_9 (and_9_out, A1in, A0in, ~B1in, ~B0in);  // And
  and and_10 (and_10_out, A1in, A0in, ~B1in, B0in);  // And
  and and_11 (and_11_out, A1in, A0in, B1in, ~B0in);  // And
  and and_12 (and_12_out, A1in, A0in, B1in, B0in);
  and and_13 (and_13_out, ~A1in, ~A0in, ~B1in, B0in);  // And
  and and_14 (and_14_out, ~A1in, ~A0in, B1in, B0in);  // And
  and and_15 (and_15_out, ~A1in, A0in, ~B1in, ~B0in);  // And
  and and_16 (and_16_out, ~A1in, A0in, ~B1in, B0in);  // And
  and and_17 (and_17_out, ~A1in, A0in, B1in, B0in);  // And
  and and_18 (and_18_out, A1in, ~A0in, B1in, B0in);  // And
  and and_19 (and_19_out, A1in, A0in, ~B1in, ~B0in);  // And
  and and_20 (and_20_out, A1in, A0in, ~B1in, B0in);  // And
  and and_21 (and_21_out, A1in, A0in, B1in, ~B0in);  // And
  and and_22 (and_22_out, A1in, A0in, B1in, B0in);
  or or_1 (or_1_out, and_1_out, and_2_out, and_3_out, and_4_out);
  or or_2 (or_2_out, and_5_out, and_6_out, and_7_out, and_8_out);
  or or_3 (or_3_out, and_9_out, and_10_out, and_11_out, and_12_out);
  or or_4 (or_4_out, and_13_out, and_14_out, and_15_out, and_16_out);
  or or_5 (or_5_out, and_17_out, and_18_out);
  or or_6 (or_6_out, and_19_out, and_20_out, and_21_out, and_22_out);
  or or_7 (out_6, or_4_out, or_5_out, or_6_out);
  or or_8 (out_5, or_1_out, or_2_out, or_3_out);

  // Notes on the sheet:
  //   Part 3: Max2
  //   R1
  //   R0
endmodule
