// Digital circuit 32bit_reg.dig as structural Verilog
module _32bit_reg (
  input  [31:0] D,
  input  C,
  input  en,
  input  clr,
  output [31:0] Q
);

  wire or_1_out;
  wire [31:0] multiplexer_1_out;

  Multiplexer #(.Bits(32)) multiplexer_1 (.sel(clr), .in_0(D), .in_1({32{1'b0}}), .out(multiplexer_1_out));
  or or_1 (or_1_out, en, clr);
  Register #(.Bits(32)) register_1 (.D(multiplexer_1_out), .C(C), .en(or_1_out), .Q(Q));
endmodule
