// Digital circuit alu.dig as structural Verilog
module alu (
  input  [2:0] ALUOp,
  input  [31:0] A,
  input  [31:0] B,
  output [31:0] R,
  output N,
  output Z,
  output C,
  output V,
  output [3:0] NZCV
);

  wire [31:0] add_1_s, barrelshifter_1_out, barrelshifter_2_out, sub_1_s;
  wire [63:0] mul_1_mul;

  Add #(.Bits(32)) add_1 (.a(A), .b(B), .c_i(1'b0), .s(add_1_s));  // open: c_o
  Sub #(.Bits(32)) sub_1 (.a(A), .b(B), .c_i(1'b0), .s(sub_1_s));  // open: c_o
  Mul #(.Bits(32)) mul_1 (.a(A), .b(B), .mul(mul_1_mul));
  BarrelShifter #(.Bits(32)) barrelshifter_1 (.in(A), .shift(B[5:0]), .out(barrelshifter_1_out));
  BarrelShifter #(.Bits(32), .direction("right")) barrelshifter_2 (.in(A), .shift(B[5:0]), .out(barrelshifter_2_out));
  Multiplexer #(.Selector_Bits(3), .Bits(32)) multiplexer_1 (
    .sel(ALUOp), .in_0(add_1_s), .in_1(sub_1_s), .in_2(mul_1_mul[31:0]), .in_3(B),
    .in_4(barrelshifter_1_out), .in_5(barrelshifter_2_out), .in_6({32{1'b0}}), .in_7({32{1'b0}}),
    .out({C, R[30:0]}));
  Comparator #(.Bits(32)) comparator_1 (.a({C, R[30:0]}), .b({32{1'b0}}), .eq(NZCV[1]));  // open: gt, lt
  and and_1 (NZCV[3], R[20], C);

  assign N = C;
  assign {NZCV[2], NZCV[0]} = {2{C}};
  assign R[31] = C;
  assign V = NZCV[3];
  assign Z = NZCV[1];

  // Notes on the sheet:
  //   good
endmodule
