// Digital circuit partial_processor.dig as structural Verilog
module partial_processor (
  input  [3:0] RR0,
  input  [3:0] RR1,
  input  [3:0] WR,
  input  WE,
  input  [2:0] ALUOp,
  input  ALUSrcB,
  input  [31:0] in_8,
  input  clk,
  input  in_10,
  output [31:0] R
);

  wire C, N, V, Z;
  wire [31:0] add_1_s, iw, multiplexer_1_out, PC_q, r0, r1, r2, r3, r4, r5, r6, r7, r8, r9, r10, r11, r12,
       r13, r14, r15, register_reg_1_rd0, register_reg_1_rd1;

  // Probe on iw
  _32bit_reg PC (.D(add_1_s), .C(clk), .en(1'b1), .clr(in_10), .Q(PC_q));
  ROM #(.AddrBits(5), .Bits(32)) rom_1 (.A(PC_q[6:2]), .sel(1'b1), .D(iw));
  Add #(.Bits(32)) add_1 (.a(PC_q), .b(32'h4), .c_i(1'b0), .s(add_1_s));  // open: c_o
  // Probe on r0
  // Probe on r2
  // Probe on r4
  // Probe on r6
  register_reg register_reg_1 (
    .ReadReg0(RR0), .ReadReg1(RR1), .WriteReg(WR), .WriteData(R), .WriteEn(WE), .PC(add_1_s), .CLK(clk),
    .CLR(in_10), .RD0(register_reg_1_rd0), .RD1(register_reg_1_rd1), .r0(r0), .r1(r1), .r2(r2), .r3(r3),
    .r4(r4), .r5(r5), .r6(r6), .r7(r7), .r8(r8), .r9(r9), .r10(r10), .r11(r11), .r12(r12), .r13(r13),
    .r14(r14), .r15(r15));
  // Probe on r1
  // Probe on r3
  // Probe on r5
  // Probe on r7
  // Probe on r8
  // Probe on r10
  // Probe on r12
  // Probe on r14
  Multiplexer #(.Bits(32)) multiplexer_1 (
    .sel(ALUSrcB), .in_0(register_reg_1_rd1), .in_1(in_8), .out(multiplexer_1_out));
  // Probe on r9
  // Probe on r11
  // Probe on r13
  // Probe on r15
  alu alu_1 (
    .ALUOp(ALUOp), .A(register_reg_1_rd0), .B(multiplexer_1_out), .R(R), .N(N), .Z(Z), .C(C), .V(V));  // open: NZCV
  // Probe on N
  // Probe on Z
  // Probe on C
  // Probe on V

  // Notes on the sheet:
  //   contents of rom_1 (hex, n*v repeats v):
  //   e2800001,e3a02002,e0800002,e2a00001,e2800000
  //   lr
  //   sp
  //   pc
endmodule
