// Digital circuit register_reg.dig as structural Verilog
module register_reg (
  input  [3:0] ReadReg0,
  input  [3:0] ReadReg1,
  input  [3:0] WriteReg,
  input  [31:0] WriteData,
  input  WriteEn,
  input  [31:0] PC,
  input  CLK,
  input  CLR,
  output [31:0] RD0,
  output [31:0] RD1,
  output [31:0] r0,
  output [31:0] r1,
  output [31:0] r2,
  output [31:0] r3,
  output [31:0] r4,
  output [31:0] r5,
  output [31:0] r6,
  output [31:0] r7,
  output [31:0] r8,
  output [31:0] r9,
  output [31:0] r10,
  output [31:0] r11,
  output [31:0] r12,
  output [31:0] r13,
  output [31:0] r14,
  output [31:0] r15
);

  wire write_reg_decoder_1_p3, write_reg_decoder_1_p4, write_reg_decoder_1_p5, write_reg_decoder_1_p6,
       write_reg_decoder_1_p7, write_reg_decoder_1_p8, write_reg_decoder_1_p9, write_reg_decoder_1_p10,
       write_reg_decoder_1_p11, write_reg_decoder_1_p12, write_reg_decoder_1_p13, write_reg_decoder_1_p14,
       write_reg_decoder_1_p15, write_reg_decoder_1_p16, write_reg_decoder_1_p17;

  // write_reg_decoder write_reg_decoder_1: pin names not known; wires that end beside it: WriteReg, WriteEn, write_reg_decoder_1_p3, write_reg_decoder_1_p4, write_reg_decoder_1_p5, write_reg_decoder_1_p6, write_reg_decoder_1_p7, write_reg_decoder_1_p8, write_reg_decoder_1_p9, write_reg_decoder_1_p10, write_reg_decoder_1_p11, write_reg_decoder_1_p12, write_reg_decoder_1_p13, write_reg_decoder_1_p14, write_reg_decoder_1_p15, write_reg_decoder_1_p16, write_reg_decoder_1_p17
  _32bit_reg _32bit_reg_1 (.D(WriteData), .C(CLK), .en(write_reg_decoder_1_p3), .clr(CLR), .Q(r0));
  _32bit_reg _32bit_reg_2 (.D(WriteData), .C(CLK), .en(write_reg_decoder_1_p4), .clr(CLR), .Q(r1));
  _32bit_reg _32bit_reg_3 (.D(WriteData), .C(CLK), .en(write_reg_decoder_1_p5), .clr(CLR), .Q(r2));
  _32bit_reg _32bit_reg_4 (.D(WriteData), .C(CLK), .en(write_reg_decoder_1_p6), .clr(CLR), .Q(r3));
  _32bit_reg _32bit_reg_5 (.D(WriteData), .C(CLK), .en(write_reg_decoder_1_p7), .clr(CLR), .Q(r4));
  _32bit_reg _32bit_reg_6 (.D(WriteData), .C(CLK), .en(write_reg_decoder_1_p8), .clr(CLR), .Q(r5));
  _32bit_reg _32bit_reg_7 (.D(WriteData), .C(CLK), .en(write_reg_decoder_1_p9), .clr(CLR), .Q(r6));
  _32bit_reg _32bit_reg_8 (.D(WriteData), .C(CLK), .en(write_reg_decoder_1_p10), .clr(CLR), .Q(r7));
  _32bit_reg _32bit_reg_9 (.D(WriteData), .C(CLK), .en(write_reg_decoder_1_p11), .clr(CLR), .Q(r8));
  _32bit_reg _32bit_reg_10 (.D(WriteData), .C(CLK), .en(write_reg_decoder_1_p12), .clr(CLR), .Q(r9));
  _32bit_reg _32bit_reg_11 (.D(WriteData), .C(CLK), .en(write_reg_decoder_1_p13), .clr(CLR), .Q(r10));
  _32bit_reg _32bit_reg_12 (.D(WriteData), .C(CLK), .en(write_reg_decoder_1_p14), .clr(CLR), .Q(r11));
  _32bit_reg _32bit_reg_13 (.D(WriteData), .C(CLK), .en(write_reg_decoder_1_p15), .clr(CLR), .Q(r12));
  _32bit_reg _32bit_reg_14 (.D(WriteData), .C(CLK), .en(write_reg_decoder_1_p16), .clr(CLR), .Q(r13));
  _32bit_reg _32bit_reg_15 (.D(WriteData), .C(CLK), .en(write_reg_decoder_1_p17), .clr(CLR), .Q(r14));
  Multiplexer #(.Selector_Bits(4), .Bits(32)) multiplexer_1 (
    .sel(ReadReg0), .in_0(r0), .in_1(r1), .in_2(r2), .in_3(r3), .in_4(r4), .in_5(r5), .in_6(r6), .in_7(r7),
    .in_8(r8), .in_9(r9), .in_10(r10), .in_11(r11), .in_12(r12), .in_13(r13), .in_14(r14), .in_15(PC),
    .out(RD0));
  Multiplexer #(.Selector_Bits(4), .Bits(32)) multiplexer_2 (
    .sel(ReadReg1), .in_0(r0), .in_1(r1), .in_2(r2), .in_3(r3), .in_4(r4), .in_5(r5), .in_6(r6), .in_7(r7),
    .in_8(r8), .in_9(r9), .in_10(r10), .in_11(r11), .in_12(r12), .in_13(r13), .in_14(r14), .in_15(PC),
    .out(RD1));

  assign r15 = PC;
endmodule
