// Digital circuit control_unit.dig as structural Verilog
module control_unit (
  input  [31:0] iw,
  input  [3:0] NZCV,
  input  CLK,
  output RFW,
  output [1:0] EXTop,
  output ALUsrcB,
  output [2:0] ALUop,
  output [1:0] PCsel,
  output [1:0] RR0sel,
  output RR1sel,
  output [1:0] WRsel,
  output WDsel,
  output MR,
  output MW
);

  wire AL_eq, and_1_out, and_2_out, and_3_out, and_4_out, and_5_out, and_6_out, C, comparator_1_eq,
       comparator_2_eq, comparator_3_eq, condex, decoder_1_csprw, EQ_eq, GE_eq, GT_eq, LT_eq, N, NE_eq,
       or_1_out, V, Z;
  wire [1:0] decoder_1_pcsel;

  Comparator #(.Bits(4)) AL (.a(iw[31:28]), .b(4'b1110), .eq(AL_eq));  // open: gt, lt
  Comparator #(.Bits(4)) NE (.a(iw[31:28]), .b(4'b0001), .eq(NE_eq));  // open: gt, lt
  Comparator #(.Bits(4)) LT (.a(iw[31:28]), .b(4'b1011), .eq(LT_eq));  // open: gt, lt
  Comparator #(.Bits(4)) EQ (.a(iw[31:28]), .b(4'b0000), .eq(EQ_eq));  // open: gt, lt
  Comparator #(.Bits(4)) GT (.a(iw[31:28]), .b(4'b1100), .eq(GT_eq));  // open: gt, lt
  Comparator #(.Bits(4)) GE (.a(iw[31:28]), .b(4'b1010), .eq(GE_eq));  // open: gt, lt
  Register #(.Bits(4)) CSPR (.D(NZCV), .C(CLK), .en(decoder_1_csprw), .Q({V, C, Z, N}));
  Comparator comparator_1 (.a(N), .b(V), .eq(comparator_1_eq));  // open: gt, lt
  Comparator comparator_2 (.a(N), .b(V), .eq(comparator_2_eq));  // open: gt, lt
  Comparator comparator_3 (.a(N), .b(V), .eq(comparator_3_eq));  // open: gt, lt
  decoder decoder_1 (
    .iw(iw), .RFW(RFW), .EXTop(EXTop), .ALUsrcB(ALUsrcB), .ALUop(ALUop), .PCsel(decoder_1_pcsel),
    .RR0sel(RR0sel), .RR1sel(RR1sel), .WRsel(WRsel), .WDsel(WDsel), .MR(MR), .MW(MW), .CSPRW(decoder_1_csprw));
  and and_1 (and_1_out, comparator_1_eq, ~Z);  // And
  or or_1 (or_1_out, comparator_2_eq, Z);
  and and_2 (and_2_out, ~Z, NE_eq);  // And
  and and_3 (and_3_out, ~comparator_3_eq, LT_eq);  // And
  and and_4 (and_4_out, Z, EQ_eq);
  and and_5 (and_5_out, and_1_out, GT_eq);
  and and_6 (and_6_out, or_1_out, GE_eq);
  or or_2 (condex, AL_eq, and_2_out, and_3_out, and_4_out, and_5_out, and_6_out);
  Multiplexer #(.Bits(2)) multiplexer_1 (.sel(condex), .in_0(2'b00), .in_1(decoder_1_pcsel), .out(PCsel));
endmodule
