// Digital circuit decoder.dig as structural Verilog
module decoder (
  input  [31:0] iw,
  output RFW,
  output [1:0] EXTop,
  output ALUsrcB,
  output [2:0] ALUop,
  output [1:0] PCsel,
  output [1:0] RR0sel,
  output RR1sel,
  output [1:0] WRsel,
  output WDsel,
  output MR,
  output MW,
  output CSPRW
);

  wire add_i_eq, add_r_eq, and_1_out, and_2_out, and_3_out, and_4_out, and_5_out, and_6_out, b_eq, bl_eq,
       bx_eq, cmp_i_eq, cmp_r_eq, comparator_1_eq, comparator_2_eq, comparator_3_eq, comparator_4_eq,
       comparator_5_eq, comparator_6_eq, comparator_7_eq, ldr_i__u__pre_eq, ldr_r__u__pre_eq, lsl_i_eq,
       lsl_r_eq, lsr_i_eq, lsr_r_eq, mov_i_eq, mov_r_eq, mul_r_eq, not_1_out, str_i__u__pre_eq,
       str_r__u__pre_eq, sub_i_eq, sub_r_eq;
  wire [4:0] priorityencoder_1_num;

  Comparator #(.Bits(8)) add_r (.a(iw[27:20]), .b(8'h8), .eq(add_r_eq));  // open: gt, lt
  Comparator #(.Bits(8)) add_i (.a(iw[27:20]), .b(8'h28), .eq(add_i_eq));  // open: gt, lt
  Comparator #(.Bits(8)) sub_r (.a(iw[27:20]), .b(8'h4), .eq(sub_r_eq));  // open: gt, lt
  Comparator #(.Bits(8)) sub_i (.a(iw[27:20]), .b(8'h24), .eq(sub_i_eq));  // open: gt, lt
  Comparator #(.Bits(8)) mov_r (.a(iw[27:20]), .b(8'h1a), .eq(mov_r_eq));  // open: gt, lt
  Comparator #(.Bits(8)) comparator_1 (.a(iw[11:4]), .b({8{1'b0}}), .eq(comparator_1_eq));  // open: gt, lt
  Comparator #(.Bits(8)) lsl_r (.a(iw[27:20]), .b(8'h1a), .eq(lsl_r_eq));  // open: gt, lt
  Comparator #(.Bits(2)) comparator_2 (.a(iw[6:5]), .b(2'b00), .eq(comparator_2_eq));  // open: gt, lt
  Comparator #(.Bits(8)) lsl_i (.a(iw[27:20]), .b(8'h1a), .eq(lsl_i_eq));  // open: gt, lt
  Comparator #(.Bits(3)) comparator_3 (.a(iw[6:4]), .b(3'b000), .eq(comparator_3_eq));  // open: gt, lt
  Comparator #(.Bits(8)) comparator_4 (.a(iw[11:4]), .b({8{1'b0}}), .eq(comparator_4_eq));  // open: gt, lt
  Comparator #(.Bits(8)) lsr_r (.a(iw[27:20]), .b(8'h1a), .eq(lsr_r_eq));  // open: gt, lt
  Comparator #(.Bits(2)) comparator_5 (.a(iw[6:5]), .b(2'b01), .eq(comparator_5_eq));  // open: gt, lt
  Comparator #(.Bits(8)) lsr_i (.a(iw[27:20]), .b(8'h1a), .eq(lsr_i_eq));  // open: gt, lt
  Comparator #(.Bits(2)) comparator_6 (.a(iw[6:5]), .b(2'b01), .eq(comparator_6_eq));  // open: gt, lt
  Comparator #(.Bits(8)) mov_i (.a(iw[27:20]), .b(8'h3a), .eq(mov_i_eq));  // open: gt, lt
  Comparator #(.Bits(4)) comparator_7 (.a(iw[11:8]), .b(4'b0000), .eq(comparator_7_eq));  // open: gt, lt
  Comparator #(.Bits(8)) cmp_r (.a(iw[27:20]), .b(8'h15), .eq(cmp_r_eq));  // open: gt, lt
  Comparator #(.Bits(8)) cmp_i (.a(iw[27:20]), .b(8'h35), .eq(cmp_i_eq));  // open: gt, lt
  Comparator #(.Bits(8)) ldr_r__u__pre (.a(iw[27:20]), .b(8'h79), .eq(ldr_r__u__pre_eq));  // open: gt, lt
  Comparator #(.Bits(8)) ldr_i__u__pre (.a(iw[27:20]), .b(8'h59), .eq(ldr_i__u__pre_eq));  // open: gt, lt
  Comparator #(.Bits(8)) str_r__u__pre (.a(iw[27:20]), .b(8'h78), .eq(str_r__u__pre_eq));  // open: gt, lt
  Comparator #(.Bits(8)) str_i__u__pre (.a(iw[27:20]), .b(8'h58), .eq(str_i__u__pre_eq));  // open: gt, lt
  Comparator #(.Bits(8)) mul_r (.a(iw[27:20]), .b({8{1'b0}}), .eq(mul_r_eq));  // open: gt, lt
  Comparator #(.Bits(4)) b (.a(iw[27:24]), .b(4'b1010), .eq(b_eq));  // open: gt, lt
  Comparator #(.Bits(4)) bl (.a(iw[27:24]), .b(4'b1011), .eq(bl_eq));  // open: gt, lt
  Comparator #(.Bits(24)) bx (.a(iw[27:4]), .b(24'h12fff1), .eq(bx_eq));  // open: gt, lt
  and and_1 (and_1_out, mov_r_eq, comparator_1_eq);
  and and_2 (and_2_out, lsl_r_eq, iw[4], comparator_2_eq);
  and and_3 (and_3_out, lsl_i_eq, comparator_3_eq, ~comparator_4_eq);  // And
  and and_4 (and_4_out, lsr_r_eq, iw[4], comparator_5_eq);
  not not_1 (not_1_out, iw[4]);
  and and_5 (and_5_out, mov_i_eq, comparator_7_eq);
  and and_6 (and_6_out, lsr_i_eq, not_1_out, comparator_6_eq);
  // Probe on iw[27:20]
  // Probe on iw[27:24]
  // Probe on iw[27:4]
  // Probe on iw[11:4]
  // Probe on iw[11:8]
  // Probe on iw[6:4]
  // Probe on iw[6:5]
  // Probe on iw[4]
  PriorityEncoder #(.Selector_Bits(5)) priorityencoder_1 (
    .in0(add_r_eq), .in1(add_i_eq), .in2(sub_r_eq), .in3(sub_i_eq), .in4(and_1_out), .in5(and_2_out),
    .in6(and_3_out), .in7(and_4_out), .in8(and_6_out), .in9(and_5_out), .in10(cmp_r_eq), .in11(cmp_i_eq),
    .in12(ldr_r__u__pre_eq), .in13(ldr_i__u__pre_eq), .in14(str_r__u__pre_eq), .in15(str_i__u__pre_eq),
    .in16(mul_r_eq), .in17(b_eq), .in18(bl_eq), .in19(bx_eq), .in20(1'b0), .in21(1'b0), .in22(1'b0),
    .in23(1'b0), .in24(1'b0), .in25(1'b0), .in26(1'b0), .in27(1'b0), .in28(1'b0), .in29(1'b0), .in30(1'b0),
    .in31(1'b0), .num(priorityencoder_1_num));  // open: any
  Multiplexer #(.Selector_Bits(5), .Bits(18)) multiplexer_1 (
    .sel(priorityencoder_1_num), .in_0(18'h20000), .in_1(18'h24000), .in_2(18'h20800), .in_3(18'h24800),
    .in_4(18'h21800), .in_5(18'h3a140), .in_6(18'h3e100), .in_7(18'h3a940), .in_8(18'h3e900),
    .in_9(18'h25800), .in_10(18'h801), .in_11(18'h4801), .in_12(18'h28004), .in_13(18'h2c004),
    .in_14(18'h8002), .in_15(18'hc002), .in_16(18'h211a0), .in_17(18'h14280), .in_18(18'h34298),
    .in_19(18'h400), .in_20({18{1'b0}}), .in_21({18{1'b0}}), .in_22({18{1'b0}}), .in_23({18{1'b0}}),
    .in_24({18{1'b0}}), .in_25({18{1'b0}}), .in_26({18{1'b0}}), .in_27({18{1'b0}}), .in_28({18{1'b0}}),
    .in_29({18{1'b0}}), .in_30({18{1'b0}}), .in_31({18{1'b0}}),
    .out({RFW, EXTop, ALUsrcB, ALUop, PCsel, RR0sel, RR1sel, WRsel, WDsel, MR, MW, CSPRW}));
  // Probe on {RFW, EXTop, ALUsrcB, ALUop, PCsel, RR0sel, RR1sel, WRsel, WDsel, MR, MW, CSPRW}
  // Probe on RFW
  // Probe on EXTop
  // Probe on ALUsrcB
  // Probe on ALUop
  // Probe on PCsel
  // Probe on RR0sel
  // Probe on RR1sel
  // Probe on WRsel
  // Probe on WDsel
  // Probe on MR
  // Probe on MW
  // Probe on CSPRW

  // Other names for the same wires on the sheet: bits4_4 = iw[4]; bits6_4[2:0] = iw[6:4]; bits11_4[7:0] = iw[11:4];
  //   bits27_4[23:0] = iw[27:4]; bits6_5[1:0] = iw[6:5]; bits11_8[3:0] = iw[11:8]; bits27_20[7:0] = iw[27:20];
  //   bits27_24[3:0] = iw[27:24]

  // Notes on the sheet:
  //   Arm Instructions: DP
  //   Arm Instructions: MEM
  //   Arm Instructions: MUL
  //   Arm Instructions: COND EXEC
endmodule
