// Digital circuit extension_unit.dig as structural Verilog
module extension_unit (
  input  [31:0] iw,
  input  [1:0] EXTop,
  output [31:0] extimm
);

  wire [31:0] barrelshifter_1_out, bitextender_1_out;

  BitExtender #(.inputBits(24), .outputBits(32)) bitextender_1 (.in(iw[23:0]), .out(bitextender_1_out));
  BarrelShifter #(.Bits(32)) barrelshifter_1 (.in(bitextender_1_out), .shift(6'b000010), .out(barrelshifter_1_out));
  Multiplexer #(.Selector_Bits(2), .Bits(32)) multiplexer_1 (
    .sel(EXTop), .in_0({{24{1'b0}}, iw[7:0]}), .in_1({{20{1'b0}}, iw[11:0]}), .in_2(barrelshifter_1_out),
    .in_3({{27{1'b0}}, iw[11:7]}), .out(extimm));

  // Notes on the sheet:
  //   DP
  //   MEM
  //   B
  //   LS
endmodule
