// Digital circuit extra_credit_register_file.dig as structural Verilog
module extra_credit_register_file (
  input  [3:0] ReadReg0,
  input  [3:0] ReadReg1,
  input  [3:0] WriteReg,
  input  [31:0] WriteData,
  input  WriteEn,
  input  [31:0] PC,
  input  CLK,
  input  CLR,
  input  [3:0] Source,
  output [31:0] RD0,
  output [31:0] RD1,
  output [31:0] r0,
  output [31:0] r1,
  output [31:0] r2,
  output [31:0] r3,
  output [31:0] r4,
  output [31:0] r5,
  output [31:0] r6,
  output [31:0] r7,
  output [31:0] r8,
  output [31:0] r9,
  output [31:0] r10,
  output [31:0] r11,
  output [31:0] r12,
  output [31:0] r13,
  output [31:0] r14,
  output [31:0] r15,
  output [31:0] SRC
);

  wire register_decoder_1_d_0, register_decoder_1_d_1, register_decoder_1_d_2, register_decoder_1_d_3,
       register_decoder_1_d_4, register_decoder_1_d_5, register_decoder_1_d_6, register_decoder_1_d_7,
       register_decoder_1_d_8, register_decoder_1_d_9, register_decoder_1_d_10, register_decoder_1_d_11,
       register_decoder_1_d_12, register_decoder_1_d_13, register_decoder_1_d_14;

  register_decoder register_decoder_1 (
    .Sel(WriteReg), .EN(WriteEn), .D_0(register_decoder_1_d_0), .D_1(register_decoder_1_d_1),
    .D_2(register_decoder_1_d_2), .D_3(register_decoder_1_d_3), .D_4(register_decoder_1_d_4),
    .D_5(register_decoder_1_d_5), .D_6(register_decoder_1_d_6), .D_7(register_decoder_1_d_7),
    .D_8(register_decoder_1_d_8), .D_9(register_decoder_1_d_9), .D_10(register_decoder_1_d_10),
    .D_11(register_decoder_1_d_11), .D_12(register_decoder_1_d_12), .D_13(register_decoder_1_d_13),
    .D_14(register_decoder_1_d_14));  // open: D_15
  // register register_1: pin names not known; wires that end beside it: WriteData, CLK, register_decoder_1_d_0, CLR, r0
  // register register_2: pin names not known; wires that end beside it: WriteData, CLK, register_decoder_1_d_1, CLR, r1
  // register register_3: pin names not known; wires that end beside it: WriteData, CLK, register_decoder_1_d_2, CLR, r2
  // register register_4: pin names not known; wires that end beside it: WriteData, CLK, register_decoder_1_d_3, CLR, r3
  // register register_5: pin names not known; wires that end beside it: WriteData, CLK, register_decoder_1_d_4, CLR, r4
  // register register_6: pin names not known; wires that end beside it: WriteData, CLK, register_decoder_1_d_5, CLR, r5
  // register register_7: pin names not known; wires that end beside it: WriteData, CLK, register_decoder_1_d_6, CLR, r6
  // register register_8: pin names not known; wires that end beside it: WriteData, CLK, register_decoder_1_d_7, CLR, r7
  // register register_9: pin names not known; wires that end beside it: WriteData, CLK, register_decoder_1_d_8, CLR, r8
  // register register_10: pin names not known; wires that end beside it: WriteData, CLK, register_decoder_1_d_9, CLR, r9
  // register register_11: pin names not known; wires that end beside it: WriteData, CLK, register_decoder_1_d_10, CLR, r10
  // register register_12: pin names not known; wires that end beside it: WriteData, CLK, register_decoder_1_d_11, CLR, r11
  // register register_13: pin names not known; wires that end beside it: WriteData, CLK, register_decoder_1_d_12, CLR, r12
  // register register_14: pin names not known; wires that end beside it: WriteData, CLK, register_decoder_1_d_13, CLR, r13
  // register register_15: pin names not known; wires that end beside it: WriteData, CLK, register_decoder_1_d_14, CLR, r14
  Multiplexer #(.Selector_Bits(4), .Bits(32)) multiplexer_1 (
    .sel(ReadReg0), .in_0(r0), .in_1(r1), .in_2(r2), .in_3(r3), .in_4(r4), .in_5(r5), .in_6(r6), .in_7(r7),
    .in_8(r8), .in_9(r9), .in_10(r10), .in_11(r11), .in_12(r12), .in_13(r13), .in_14(r14), .in_15(PC),
    .out(RD0));
  Multiplexer #(.Selector_Bits(4), .Bits(32)) multiplexer_2 (
    .sel(ReadReg1), .in_0(r0), .in_1(r1), .in_2(r2), .in_3(r3), .in_4(r4), .in_5(r5), .in_6(r6), .in_7(r7),
    .in_8(r8), .in_9(r9), .in_10(r10), .in_11(r11), .in_12(r12), .in_13(r13), .in_14(r14), .in_15(PC),
    .out(RD1));
  Multiplexer #(.Selector_Bits(4), .Bits(32)) multiplexer_3 (
    .sel(Source), .in_0(r0), .in_1(r1), .in_2(r2), .in_3(r3), .in_4(r4), .in_5(r5), .in_6(r6), .in_7(r7),
    .in_8(r8), .in_9(r9), .in_10(r10), .in_11(r11), .in_12(r12), .in_13(r13), .in_14(r14), .in_15(PC),
    .out(SRC));

  assign r15 = PC;
endmodule
