// Digital circuit instruction_memory.dig as structural Verilog
module instruction_memory (
  input  [7:0] Addr,
  input  [2:0] Prog,
  output [31:0] D
);

  wire [31:0] factorial_d, quadratic_d, search_d, sort_d, sum_array_d;

  ROM #(.AddrBits(8), .Bits(32)) quadratic (.A(Addr), .sel(1'b1), .D(quadratic_d));
  ROM #(.AddrBits(8), .Bits(32)) factorial (.A(Addr), .sel(1'b1), .D(factorial_d));
  ROM #(.AddrBits(8), .Bits(32)) sum_array (.A(Addr), .sel(1'b1), .D(sum_array_d));
  ROM #(.AddrBits(8), .Bits(32)) search (.A(Addr), .sel(1'b1), .D(search_d));
  ROM #(.AddrBits(8), .Bits(32)) sort (.A(Addr), .sel(1'b1), .D(sort_d));
  Multiplexer #(.Selector_Bits(3), .Bits(32)) multiplexer_1 (
    .sel(Prog), .in_0(quadratic_d), .in_1(factorial_d), .in_2(sum_array_d), .in_3(search_d), .in_4(sort_d),
    .in_5({32{1'b0}}), .in_6({32{1'b0}}), .in_7({32{1'b0}}), .out(D));

  // Notes on the sheet:
  //   contents of quadratic (hex, n*v repeats v):
  //   e3a00002,e3a01004,e3a02008,e3a03010,eb000000,e2800000,e00c0090,e001019c,e0020290,
  //   e0810002,e0800003,e12fff1e
  //   contents of factorial (hex, n*v repeats v):
  //   e3a00001,e1a0d500,e3a00005,eb000000,e2800000,e24dd008,e58de000,e3500000,1a000001,
  //   e3a00001,ea000004,e58d0004,e2400001,ebfffff6,e59d1004,e0000091,e59de000,e28dd008,
  //   e12fff1e
  //   contents of sum_array (hex, n*v repeats v):
  //   e3a00001,e1a0d500,e24dd014,e3a00000,e58d0000,e3a00004,e58d0004,e3a00008,e58d0008,
  //   e3a0000c,e58d000c,e3a00010,e58d0010,e1a0000d,e3a01005,eb000001,e28dd014,e2800000,
  //   e3a02000,e3a03000,e1530001,aa000004,e590c000,e082200c,e2800004,e2833001,eafffff8,
  //   e1a00002,e12fff1e
  //   contents of search (hex, n*v repeats v):
  //   e3a00001,e1a0d500,e24dd014,e3a00000,e58d0000,e3a00004,e58d0004,e3a00008,e58d0008,
  //   e3a0000c,e58d000c,e3a00010,e58d0010,e1a0000d,e3a01000,e3a02005,e3a0300c,eb000001,
  //   e28dd014,e2800000,e24dd004,e58de000,e1520001,ba000011,e0424001,e1a040a4,e0814004,
  //   e1a06104,e7905006,e1550003,a000001,ca000002,ea000004,e1a00004,ea000007,e2444001,e1a02004,
  //   ea000001,e2844001,e1a01004,ebffffea,ea000000,e3e00000,e59de000,e28dd004,e12fff1e
  //   contents of sort (hex, n*v repeats v):
  //   e3a00001,e1a0d500,e24dd014,e3a00010,e58d0000,e3a00004,e58d0004,e3a00020,e58d0008,
  //   e3a00002,e58d000c,e3a00008,e58d0010,e1a0000d,e3a01005,eb000013,e28dd014,e2800000,
  //   e5903000,e3a02000,e3a04000,ea000009,e1520001,ba000000,ea000008,e1a06102,e7905006,
  //   e1550003,ca000000,ea000001,e1a03005,e1a04002,e2822001,eafffff3,e1a00004,e12fff1e,
  //   e24dd010,e58de000,e3a02000,e1520001,ba000000,ea000016,e58d0004,e58d1008,e58d200c,
  //   e1a04102,e0800004,e0411002,ebffffe0,e1a05003,e1a03000,e59d200c,e59d1008,e59d0004,
  //   e0833002,e1530002,1a000000,ea000004,e1a06102,e7904006,e7805006,e1a06103,e7804006,
  //   e2822001,eaffffe5,e1a00001,e59de000,e28dd010,e12fff1e
endmodule
