// Digital circuit partial_processor.dig as structural Verilog
module partial_processor (
  input  clk,
  input  [2:0] Prog,
  output [31:0] R
);

  wire a_mul, ALUsrcB, and_3_out, and_4_out, and_5_out, and_6_out, and_7_out, and_8_out, and_9_out,
       and_10_out, C, CLK_t, CLR, comparator_1_eq, comparator_2_eq, comparator_4_eq, comparator_5_eq,
       comparator_6_eq, comparator_7_eq, comparator_8_eq, comparator_9_eq, comparator_10_eq,
       comparator_11_eq, done, en, i_dp, MR, MW, N, RFW, RR1sel, V, WDsel, Z;
  wire [1:0] EXTop, PCsel, RR0sel, WRsel;
  wire [2:0] ALUOp;
  wire [3:0] cond, multiplexer_2_out, multiplexer_3_out, multiplexer_4_out, NZCV;
  wire [7:0] PC_p5_2, sp__plus__off_out;
  wire [23:0] b_offset;
  wire [27:24] iw;
  wire [31:0] add_1_s, add_2_s, Data_Memory_d, demultiplexer_1_out_0, demultiplexer_1_out_1,
       demultiplexer_1_out_2, demultiplexer_1_out_3, demultiplexer_1_out_4, demultiplexer_1_out_5,
       demultiplexer_1_out_6, demultiplexer_1_out_7, extension_unit_1_extimm, multiplexer_5_out,
       multiplexer_6_out, multiplexer_7_out, multiplexer_8_out, multiplexer_9_out, PC_p1, PC_p5, r0, r1, r2,
       r3, r4, r5, r6, r7, r8, r9, r10, r11, r12, r13, r14, r15, register_1_q, register_2_q, register_3_q,
       register_4_q, register_5_q, register_6_q, register_7_q, register_8_q, register_file_1_rd0,
       register_file_1_rd1;

  // register PC: pin names not known; wires that end beside it: PC_p1, CLK_t, 1'b1, CLR, {PC_p5[31:10], PC_p5_2, PC_p5[1:0]}
  Multiplexer #(.Selector_Bits(2), .Bits(32)) multiplexer_1 (
    .sel(PCsel), .in_0(add_1_s), .in_1(multiplexer_8_out), .in_2(register_file_1_rd1), .in_3({32{1'b0}}),
    .out(PC_p1));
  and and_1 (CLK_t, clk, ~done);  // And
  DipSwitch #(.dipDefault("true")) u_clr (.out(CLR));
  Add #(.Bits(32)) add_1 (.a({PC_p5[31:10], PC_p5_2, PC_p5[1:0]}), .b(32'h4), .c_i(1'b0), .s(add_1_s));  // open: c_o
  // Probe on {cond, iw[27:26], i_dp, iw[24], b_offset[23:22], a_mul, b_offset[20:0]}
  instruction_memory instruction_memory_1 (
    .Addr(PC_p5_2), .Prog(Prog), .D({cond, iw[27:26], i_dp, iw[24], b_offset[23:22], a_mul, b_offset[20:0]}));
  control_unit control_unit_1 (
    .iw({cond, iw[27:26], i_dp, iw[24], b_offset[23:22], a_mul, b_offset[20:0]}), .NZCV(NZCV), .CLK(CLK_t),
    .RFW(RFW), .EXTop(EXTop), .ALUsrcB(ALUsrcB), .ALUop(ALUOp), .PCsel(PCsel), .RR0sel(RR0sel),
    .RR1sel(RR1sel), .WRsel(WRsel), .WDsel(WDsel), .MR(MR), .MW(MW));
  // Probe on r0
  // Probe on r2
  // Probe on r4
  // Probe on r6
  Add #(.Bits(32)) add_2 (.a(add_1_s), .b(32'h4), .c_i(1'b0), .s(add_2_s));  // open: c_o
  // Probe on cond
  // Probe on cond
  // Probe on cond
  // Probe on cond
  // Probe on r1
  // Probe on r3
  // Probe on r5
  // Probe on r7
  // Probe on iw[27:26]
  // Probe on {iw[27:26], i_dp, iw[24], b_offset[23]}
  // Probe on iw[27:26]
  // Probe on {iw[27:26], i_dp}
  Multiplexer #(.Selector_Bits(2), .Bits(4)) multiplexer_2 (
    .sel(RR0sel), .in_0(b_offset[19:16]), .in_1(4'b1111), .in_2(b_offset[3:0]), .in_3(b_offset[11:8]),
    .out(multiplexer_2_out));
  Multiplexer #(.Bits(4)) multiplexer_3 (
    .sel(RR1sel), .in_0(b_offset[3:0]), .in_1(b_offset[11:8]), .out(multiplexer_3_out));
  Multiplexer #(.Selector_Bits(2), .Bits(4)) multiplexer_4 (
    .sel(WRsel), .in_0(b_offset[15:12]), .in_1(4'b1110), .in_2(b_offset[19:16]), .in_3(4'b0000),
    .out(multiplexer_4_out));
  Multiplexer #(.Bits(32)) multiplexer_5 (
    .sel(WDsel), .in_0(multiplexer_8_out), .in_1(add_1_s), .out(multiplexer_5_out));
  // Probe on i_dp
  // Probe on a_mul
  // Probe on i_dp
  // Probe on iw[24]
  // Probe on r8
  // Probe on r10
  // Probe on r12
  // Probe on r14
  register_file register_file_1 (
    .ReadReg0(multiplexer_2_out), .ReadReg1(multiplexer_3_out), .WriteReg(multiplexer_4_out),
    .WriteData(multiplexer_5_out), .WriteEn(RFW), .PC(add_2_s), .CLK(CLK_t), .CLR(CLR),
    .RD0(register_file_1_rd0), .RD1(register_file_1_rd1), .r0(r0), .r1(r1), .r2(r2), .r3(r3), .r4(r4),
    .r5(r5), .r6(r6), .r7(r7), .r8(r8), .r9(r9), .r10(r10), .r11(r11), .r12(r12), .r13(r13), .r14(r14),
    .r15(r15));
  // Probe on {iw[24], b_offset[23:22], a_mul}
  // Probe on b_offset[20]
  // Probe on iw[24]
  // Probe on {b_offset[23:22], a_mul, b_offset[20:0]}
  Multiplexer #(.Bits(32), .Selector_Bits(4)) multiplexer_6 (
    .sel(b_offset[15:12]), .in_0(r0), .in_1(r1), .in_2(r2), .in_3(r3), .in_4(r4), .in_5(r5), .in_6(r6),
    .in_7(r7), .in_8(r8), .in_9(r9), .in_10(r10), .in_11(r11), .in_12(r12), .in_13(r13), .in_14(r14),
    .in_15(r15), .out(multiplexer_6_out));
  // Probe on r9
  // Probe on r11
  // Probe on r13
  // Probe on r15
  // Probe on b_offset[20]
  // Probe on b_offset[19:16]
  // Probe on b_offset[23]
  // Probe on N
  // Probe on Z
  // Probe on C
  // Probe on V
  // Probe on b_offset[19:16]
  // Probe on b_offset[15:12]
  // Probe on b_offset[22]
  Multiplexer #(.Bits(32)) multiplexer_7 (
    .sel(ALUsrcB), .in_0(register_file_1_rd1), .in_1(extension_unit_1_extimm), .out(multiplexer_7_out));
  extension_unit extension_unit_1 (
    .iw({cond, iw[27:26], i_dp, iw[24], b_offset[23:22], a_mul, b_offset[20:0]}), .EXTop(EXTop),
    .extimm(extension_unit_1_extimm));
  // Probe on b_offset[15:12]
  // Probe on b_offset[11:8]
  // Probe on a_mul
  Comparator #(.Bits(32)) comparator_1 (
    .a({cond, iw[27:26], i_dp, iw[24], b_offset[23:22], a_mul, b_offset[20:0]}), .b(32'he1530002),
    .eq(comparator_1_eq));  // open: gt, lt
  Comparator #(.Bits(3)) comparator_2 (.a(Prog), .b(3'b100), .eq(comparator_2_eq));  // open: gt, lt
  alu alu_1 (
    .ALUOp(ALUOp), .A(register_file_1_rd0), .B(multiplexer_7_out), .R(R), .NZCV(NZCV), .N(N), .Z(Z), .C(C),
    .V(V));
  and and_2 (en, comparator_1_eq, comparator_2_eq);
  Comparator #(.Bits(32)) comparator_3 (
    .a({cond, iw[27:26], i_dp, iw[24], b_offset[23:22], a_mul, b_offset[20:0]}), .b(32'he2800000), .eq(done));  // open: gt, lt
  // Probe on b_offset[3:0]
  // Probe on b_offset[7:0]
  // Probe on b_offset[7:4]
  // Probe on b_offset[20]
  BarrelShifter #(.Bits(8)) sp__plus__off (.in(R[7:0]), .shift(4'b0010), .out(sp__plus__off_out));
  // Probe on extension_unit_1_extimm
  Multiplexer #(.Bits(32)) multiplexer_8 (.sel(MR), .in_0(R), .in_1(Data_Memory_d), .out(multiplexer_8_out));
  // Probe on b_offset[3:0]
  // Probe on b_offset[19:16]
  Multiplexer #(.Bits(32)) multiplexer_9 (.sel(en), .in_0({32{1'b0}}), .in_1(r5), .out(multiplexer_9_out));
  LED led_1 (.in(done));
  Demultiplexer #(.Bits(32), .Selector_Bits(3)) demultiplexer_1 (
    .sel(r2[2:0]), .in(multiplexer_9_out), .out_0(demultiplexer_1_out_0), .out_1(demultiplexer_1_out_1),
    .out_2(demultiplexer_1_out_2), .out_3(demultiplexer_1_out_3), .out_4(demultiplexer_1_out_4),
    .out_5(demultiplexer_1_out_5), .out_6(demultiplexer_1_out_6), .out_7(demultiplexer_1_out_7));
  RAMDualPort #(.AddrBits(8), .Bits(32)) Data_Memory (
    .A(sp__plus__off_out), .Din(multiplexer_6_out), .str(MW), .C(CLK_t), .ld(MR), .D(Data_Memory_d));
  // Probe on b_offset[15:12]
  // Probe on b_offset[3:0]
  // Probe on b_offset[11:0]
  Comparator #(.Bits(3)) comparator_4 (.a(r2[2:0]), .b(3'b000), .eq(comparator_4_eq));  // open: gt, lt
  Comparator #(.Bits(3)) comparator_5 (.a(r2[2:0]), .b(3'b001), .eq(comparator_5_eq));  // open: gt, lt
  Comparator #(.Bits(3)) comparator_6 (.a(r2[2:0]), .b(3'b010), .eq(comparator_6_eq));  // open: gt, lt
  Comparator #(.Bits(3)) comparator_7 (.a(r2[2:0]), .b(3'b011), .eq(comparator_7_eq));  // open: gt, lt
  Comparator #(.Bits(3)) comparator_8 (.a(r2[2:0]), .b(3'b100), .eq(comparator_8_eq));  // open: gt, lt
  Comparator #(.Bits(3)) comparator_9 (.a(r2[2:0]), .b(3'b101), .eq(comparator_9_eq));  // open: gt, lt
  Comparator #(.Bits(3)) comparator_10 (.a(r2[2:0]), .b(3'b110), .eq(comparator_10_eq));  // open: gt, lt
  Comparator #(.Bits(3)) comparator_11 (.a(r2[2:0]), .b(3'b111), .eq(comparator_11_eq));  // open: gt, lt
  and and_3 (and_3_out, comparator_4_eq, en);
  and and_4 (and_4_out, comparator_5_eq, en);
  and and_5 (and_5_out, comparator_6_eq, en);
  and and_6 (and_6_out, comparator_7_eq, en);
  and and_7 (and_7_out, comparator_8_eq, en);
  and and_8 (and_8_out, comparator_9_eq, en);
  and and_9 (and_9_out, comparator_10_eq, en);
  and and_10 (and_10_out, comparator_11_eq, en);
  Register #(.Bits(32)) register_1 (.D(demultiplexer_1_out_0), .C(CLK_t), .en(and_3_out), .Q(register_1_q));
  Register #(.Bits(32)) register_2 (.D(demultiplexer_1_out_1), .C(CLK_t), .en(and_4_out), .Q(register_2_q));
  Register #(.Bits(32)) register_3 (.D(demultiplexer_1_out_2), .C(CLK_t), .en(and_5_out), .Q(register_3_q));
  Register #(.Bits(32)) register_4 (.D(demultiplexer_1_out_3), .C(CLK_t), .en(and_6_out), .Q(register_4_q));
  Register #(.Bits(32)) register_5 (.D(demultiplexer_1_out_4), .C(CLK_t), .en(and_7_out), .Q(register_5_q));
  Register #(.Bits(32)) register_6 (.D(demultiplexer_1_out_5), .C(CLK_t), .en(and_8_out), .Q(register_6_q));
  Register #(.Bits(32)) register_7 (.D(demultiplexer_1_out_6), .C(CLK_t), .en(and_9_out), .Q(register_7_q));
  Register #(.Bits(32)) register_8 (.D(demultiplexer_1_out_7), .C(CLK_t), .en(and_10_out), .Q(register_8_q));
  // Probe on register_1_q
  // Probe on register_2_q
  // Probe on register_3_q
  // Probe on register_4_q
  // Probe on register_5_q
  // Probe on register_6_q
  // Probe on register_7_q
  // Probe on register_8_q

  // Other names for the same wires on the sheet: imm[7:0] = b_offset[7:0]; immoff[11:0] = b_offset[11:0];
  //   iw (some bits) = {cond, i_dp, b_offset[23:22], a_mul, b_offset[20:0]}; rm[3:0] = b_offset[3:0];
  //   rm_mul[3:0] = b_offset[3:0]; opmul4[3:0] = b_offset[7:4]; rs_mul[3:0] = b_offset[11:8];
  //   rd[3:0] = b_offset[15:12]; rn_mul[3:0] = b_offset[15:12]; rd_mul[3:0] = b_offset[19:16];
  //   rn[3:0] = b_offset[19:16]; l_sdt = b_offset[20]; s_dp = b_offset[20]; s_mul = b_offset[20];
  //   b_offset[21] = a_mul; opc[3:0] = {iw[24], b_offset[23:22], a_mul}; w_sdt = a_mul; b_sdt = b_offset[22];
  //   opmul6[4:0] = {iw[27:26], i_dp, iw[24], b_offset[23]}; u_sdt = b_offset[23]; l_b = iw[24]; p_sdt = iw[24];
  //   i_sdt = i_dp; opb3[2:0] = {iw[27:26], i_dp}; op2[1:0] = iw[27:26]; opmul2[1:0] = iw[27:26]; sel[2:0] = r2[2:0]

  // Notes on the sheet:
  //   clk: Hz: 2
  //   DP
  //   MUL
  //   SDT
  //   B
  //   lr
  //   sp
  //   pc
  //   Array values being stored at i from 0 to 4 for sort
  //   16
  //   4
  //   32
  //   2
  //   8
  //   unused
endmodule
