// Digital circuit register_decoder.dig as structural Verilog
module register_decoder (
  input  [3:0] Sel,
  input  EN,
  output D_0,
  output D_1,
  output D_2,
  output D_3,
  output D_4,
  output D_5,
  output D_6,
  output D_7,
  output D_8,
  output D_9,
  output D_10,
  output D_11,
  output D_12,
  output D_13,
  output D_14,
  output D_15
);

  wire decoder_1_out_0, decoder_1_out_1, decoder_1_out_2, decoder_1_out_3, decoder_1_out_4, decoder_1_out_5,
       decoder_1_out_6, decoder_1_out_7, decoder_1_out_8, decoder_1_out_9, decoder_1_out_10,
       decoder_1_out_11, decoder_1_out_12, decoder_1_out_13, decoder_1_out_14, decoder_1_out_15;

  Decoder #(.Selector_Bits(4)) decoder_1 (
    .sel(Sel), .out_0(decoder_1_out_0), .out_1(decoder_1_out_1), .out_2(decoder_1_out_2),
    .out_3(decoder_1_out_3), .out_4(decoder_1_out_4), .out_5(decoder_1_out_5), .out_6(decoder_1_out_6),
    .out_7(decoder_1_out_7), .out_8(decoder_1_out_8), .out_9(decoder_1_out_9), .out_10(decoder_1_out_10),
    .out_11(decoder_1_out_11), .out_12(decoder_1_out_12), .out_13(decoder_1_out_13),
    .out_14(decoder_1_out_14), .out_15(decoder_1_out_15));
  and and_1 (D_0, decoder_1_out_0, EN);
  and and_2 (D_1, decoder_1_out_1, EN);
  and and_3 (D_2, decoder_1_out_2, EN);
  and and_4 (D_3, decoder_1_out_3, EN);
  and and_5 (D_4, decoder_1_out_4, EN);
  and and_6 (D_5, decoder_1_out_5, EN);
  and and_7 (D_6, decoder_1_out_6, EN);
  and and_8 (D_7, decoder_1_out_7, EN);
  and and_9 (D_8, decoder_1_out_8, EN);
  and and_10 (D_9, decoder_1_out_9, EN);
  and and_11 (D_10, decoder_1_out_10, EN);
  and and_12 (D_11, decoder_1_out_11, EN);
  and and_13 (D_12, decoder_1_out_12, EN);
  and and_14 (D_13, decoder_1_out_13, EN);
  and and_15 (D_14, decoder_1_out_14, EN);
  and and_16 (D_15, decoder_1_out_15, EN);
endmodule
