// Digital circuit 16BitCounter.dig as structural Verilog
module _16BitCounter (
  input  CLK,
  input  CLR,
  output [15:0] COUNT
);

  wire [15:0] _16bitfulladder_1_sum;

  _16BitRegister _16bitregister_1 (.D(_16bitfulladder_1_sum), .CLK(CLK), .CLR(CLR), .Q(COUNT));
  _16BitFullAdder _16bitfulladder_1 (.Sum(_16bitfulladder_1_sum), .C_in(1'b0), .a(COUNT), .b(16'h1));  // open: C_out
endmodule
