// Digital circuit 16BitFullAdder.dig as structural Verilog
module _16BitFullAdder (
  input  C_in,
  input  [15:0] a,
  input  [15:0] b,
  output [15:0] Sum,
  output C_out
);

  wire _8bitfulladder_1_c_out;

  _8BitFullAdder _8bitfulladder_1 (.C_out(_8bitfulladder_1_c_out), .Sum(Sum[7:0]), .C_in(C_in), .a(a[7:0]), .b(b[7:0]));
  _8BitFullAdder _8bitfulladder_2 (
    .C_out(C_out), .Sum(Sum[15:8]), .C_in(_8bitfulladder_1_c_out), .a(a[15:8]), .b(b[15:8]));
endmodule
