// Digital circuit 16BitRegister.dig as structural Verilog
module _16BitRegister (
  input  [15:0] D,
  input  CLK,
  input  CLR,
  output [15:0] Q
);

  _8BitRegister _8bitregister_1 (.D(D[7:0]), .CLK(CLK), .CLR(CLR), .Q(Q[7:0]));
  _8BitRegister _8bitregister_2 (.D(D[15:8]), .CLK(CLK), .CLR(CLR), .Q(Q[15:8]));
endmodule
