// Digital circuit 24BitComparator.dig as structural Verilog
module _24BitComparator (
  input  [23:0] a,
  input  [23:0] b,
  output eq
);

  wire _8bitcomparator_1_eq, _8bitcomparator_2_eq, _8bitcomparator_3_eq;

  _8BitComparator _8bitcomparator_1 (.a(a[7:0]), .b(b[7:0]), .eq(_8bitcomparator_1_eq));
  _8BitComparator _8bitcomparator_2 (.a(a[15:8]), .b(b[15:8]), .eq(_8bitcomparator_2_eq));
  _8BitComparator _8bitcomparator_3 (.a(a[23:16]), .b(b[23:16]), .eq(_8bitcomparator_3_eq));
  and and_1 (eq, _8bitcomparator_1_eq, _8bitcomparator_2_eq, _8bitcomparator_3_eq);
endmodule
