// Digital circuit 2BitComparator.dig as structural Verilog
module _2BitComparator (
  input  [1:0] a,
  input  [1:0] b,
  output eq
);

  wire xnor_1_out, xnor_2_out;

  xnor xnor_1 (xnor_1_out, a[0], b[0]);
  xnor xnor_2 (xnor_2_out, a[1], b[1]);
  and and_1 (eq, xnor_1_out, xnor_2_out);
endmodule
