// Digital circuit 32BitComparator.dig as structural Verilog
module _32BitComparator (
  input  [31:0] a,
  input  [31:0] b,
  output eq
);

  wire _8bitcomparator_1_eq, _24bitcomparator_1_eq;

  _24BitComparator _24bitcomparator_1 (.a(a[23:0]), .b(b[23:0]), .eq(_24bitcomparator_1_eq));
  _8BitComparator _8bitcomparator_1 (.a(a[31:24]), .b(b[31:24]), .eq(_8bitcomparator_1_eq));
  and and_1 (eq, _24bitcomparator_1_eq, _8bitcomparator_1_eq);
endmodule
