// Digital circuit 4BitComparator.dig as structural Verilog
module _4BitComparator (
  input  [3:0] a,
  input  [3:0] b,
  output eq
);

  wire _2bitcomparator_1_eq, _2bitcomparator_2_eq;

  _2BitComparator _2bitcomparator_1 (.a(a[1:0]), .b(b[1:0]), .eq(_2bitcomparator_1_eq));
  _2BitComparator _2bitcomparator_2 (.a(a[3:2]), .b(b[3:2]), .eq(_2bitcomparator_2_eq));
  and and_1 (eq, _2bitcomparator_1_eq, _2bitcomparator_2_eq);
endmodule
