// Digital circuit 8BitComparator.dig as structural Verilog
module _8BitComparator (
  input  [7:0] a,
  input  [7:0] b,
  output eq
);

  wire _4bitcomparator_1_eq, _4bitcomparator_2_eq;

  _4BitComparator _4bitcomparator_1 (.a(a[3:0]), .b(b[3:0]), .eq(_4bitcomparator_1_eq));
  _4BitComparator _4bitcomparator_2 (.a(a[7:4]), .b(b[7:4]), .eq(_4bitcomparator_2_eq));
  and and_1 (eq, _4bitcomparator_1_eq, _4bitcomparator_2_eq);
endmodule
