// Digital circuit 8BitFullAdder.dig as structural Verilog
module _8BitFullAdder (
  input  C_in,
  input  [7:0] a,
  input  [7:0] b,
  output C_out,
  output [7:0] Sum
);

  wire _1bitfulladder_1_c_out, _1bitfulladder_2_c_out, _1bitfulladder_3_c_out, _1bitfulladder_4_c_out,
       _1bitfulladder_5_c_out, _1bitfulladder_6_c_out, _1bitfulladder_7_c_out;

  _1BitFullAdder _1bitfulladder_1 (.a(a[0]), .b(b[0]), .C_in(C_in), .Sum(Sum[0]), .C_out(_1bitfulladder_1_c_out));
  _1BitFullAdder _1bitfulladder_2 (
    .a(a[1]), .b(b[1]), .C_in(_1bitfulladder_1_c_out), .Sum(Sum[1]), .C_out(_1bitfulladder_2_c_out));
  _1BitFullAdder _1bitfulladder_3 (
    .a(a[2]), .b(b[2]), .C_in(_1bitfulladder_2_c_out), .Sum(Sum[2]), .C_out(_1bitfulladder_3_c_out));
  _1BitFullAdder _1bitfulladder_4 (
    .a(a[3]), .b(b[3]), .C_in(_1bitfulladder_3_c_out), .Sum(Sum[3]), .C_out(_1bitfulladder_4_c_out));
  _1BitFullAdder _1bitfulladder_5 (
    .a(a[4]), .b(b[4]), .C_in(_1bitfulladder_4_c_out), .Sum(Sum[4]), .C_out(_1bitfulladder_5_c_out));
  _1BitFullAdder _1bitfulladder_6 (
    .a(a[5]), .b(b[5]), .C_in(_1bitfulladder_5_c_out), .Sum(Sum[5]), .C_out(_1bitfulladder_6_c_out));
  _1BitFullAdder _1bitfulladder_7 (
    .a(a[6]), .b(b[6]), .C_in(_1bitfulladder_6_c_out), .Sum(Sum[6]), .C_out(_1bitfulladder_7_c_out));
  _1BitFullAdder _1bitfulladder_8 (.a(a[7]), .b(b[7]), .C_in(_1bitfulladder_7_c_out), .Sum(Sum[7]), .C_out(C_out));
endmodule
