// Digital circuit 8BitRegister.dig as structural Verilog
module _8BitRegister (
  input  CLK,
  input  CLR,
  input  [7:0] D,
  output [7:0] Q
);

  d_flipflop_clr d_flipflop_clr_1 (.D(D[0]), .CLK(CLK), .CLR(CLR), .Q(Q[0]));
  d_flipflop_clr d_flipflop_clr_2 (.D(D[1]), .CLK(CLK), .CLR(CLR), .Q(Q[1]));
  d_flipflop_clr d_flipflop_clr_3 (.D(D[2]), .CLK(CLK), .CLR(CLR), .Q(Q[2]));
  d_flipflop_clr d_flipflop_clr_4 (.D(D[3]), .CLK(CLK), .CLR(CLR), .Q(Q[3]));
  d_flipflop_clr d_flipflop_clr_5 (.D(D[4]), .CLK(CLK), .CLR(CLR), .Q(Q[4]));
  d_flipflop_clr d_flipflop_clr_6 (.D(D[5]), .CLK(CLK), .CLR(CLR), .Q(Q[5]));
  d_flipflop_clr d_flipflop_clr_7 (.D(D[6]), .CLK(CLK), .CLR(CLR), .Q(Q[6]));
  d_flipflop_clr d_flipflop_clr_8 (.D(D[7]), .CLK(CLK), .CLR(CLR), .Q(Q[7]));
endmodule
