// Digital circuit Decoder.dig as structural Verilog
module Decoder (
  input  [31:0] IW,
  output [2:0] \type 
);

  wire _2bitcomparator_1_eq, _2bitcomparator_2_eq, _4bitcomparator_1_eq, _4bitcomparator_2_eq,
       _8bitcomparator_1_eq, _24bitcomparator_1_eq, and_1_out;

  _24BitComparator _24bitcomparator_1 (.a(IW[27:4]), .b(24'h12fff1), .eq(_24bitcomparator_1_eq));
  _8BitComparator _8bitcomparator_1 (.a({2'b00, IW[27:22]}), .b({8{1'b0}}), .eq(_8bitcomparator_1_eq));
  _4BitComparator _4bitcomparator_1 (.a(IW[7:4]), .b(4'b1001), .eq(_4bitcomparator_1_eq));
  _4BitComparator _4bitcomparator_2 (.a({1'b0, IW[27:25]}), .b(4'b0101), .eq(_4bitcomparator_2_eq));
  _2BitComparator _2bitcomparator_1 (.a(IW[27:26]), .b(2'b01), .eq(_2bitcomparator_1_eq));
  _2BitComparator _2bitcomparator_2 (.a(IW[27:26]), .b(2'b00), .eq(_2bitcomparator_2_eq));
  and and_1 (and_1_out, _8bitcomparator_1_eq, _4bitcomparator_1_eq);
  PriorityEncoder #(.Selector_Bits(3)) priorityencoder_1 (
    .in0(_2bitcomparator_2_eq), .in1(_2bitcomparator_1_eq), .in2(_4bitcomparator_2_eq), .in3(and_1_out),
    .in4(_24bitcomparator_1_eq), .in5(1'b0), .in6(1'b0), .in7(1'b0), .num(\type ));  // open: any

  // Notes on the sheet:
  //   bx
  //   mul
  //   branch
  //   mem
  //   dp
endmodule
