// Digital circuit InstructionMemory.dig as structural Verilog
module InstructionMemory (
  input  [7:0] A,
  input  PN,
  output [31:0] D
);

  wire [31:0] quad_d, rev_d;

  ROM #(.AddrBits(8), .Bits(32)) quad (.A(A), .sel(1'b1), .D(quad_d));
  ROM #(.AddrBits(8), .Bits(32)) rev (.A(A), .sel(1'b1), .D(rev_d));
  Multiplexer #(.Bits(32)) multiplexer_1 (.sel(PN), .in_0(quad_d), .in_1(rev_d), .out(D));

  // Notes on the sheet:
  //   contents of quad (hex, n*v repeats v):
  //   e00c0090,e001019c,e0020290,e0810002,e0800003,e12fff1e,e2800000
  //   contents of rev (hex, n*v repeats v):
  //   e1a01000,e5d12000,e3520000,a000001,e2811001,eafffffa,e2411001,e1500001,aa000006,e5d02000,
  //   e5d13000,e5c12000,e5c03000,e2800001,e2411001,eafffff6,e12fff1e,e2800000
endmodule
