// Digital circuit StaticAnalyzer.dig as structural Verilog
module StaticAnalyzer (
  input  PN,
  input  CLK,
  output [15:0] Inst_Count,
  output [15:0] DP_Count,
  output [15:0] MEM_Count,
  output [15:0] Branch_Count,
  output [15:0] MUL_Count,
  output [15:0] BX_Count
);

  wire _32bitcomparator_1_eq, and_1_out, CLR_out, decoder_2_out_0, decoder_2_out_1, decoder_2_out_2,
       decoder_2_out_3, decoder_2_out_4;
  wire [2:0] decoder_1_type;
  wire [15:0] _16bitfulladder_1_sum, multiplexer_1_out, multiplexer_2_out, multiplexer_3_out,
       multiplexer_4_out, multiplexer_5_out, multiplexer_6_out;
  wire [31:0] instructionmemory_1_d;

  DipSwitch #(.dipDefault("true")) CLR (.out(CLR_out));
  and and_1 (and_1_out, CLK, ~_32bitcomparator_1_eq);  // And
  _16BitCounter _16bitcounter_1 (.CLK(and_1_out), .CLR(CLR_out), .COUNT(Inst_Count));
  InstructionMemory instructionmemory_1 (.D(instructionmemory_1_d), .A(Inst_Count[7:0]), .PN(PN));
  _32BitComparator _32bitcomparator_1 (.a(instructionmemory_1_d), .b(32'he2800000), .eq(_32bitcomparator_1_eq));
  Decoder decoder_1 (.IW(instructionmemory_1_d), .\type (decoder_1_type));
  _16BitFullAdder _16bitfulladder_1 (
    .Sum(_16bitfulladder_1_sum), .C_in(1'b0), .a(16'h1), .b(multiplexer_6_out));  // open: C_out
  Decoder #(.Selector_Bits(3)) decoder_2 (
    .sel(decoder_1_type), .out_0(decoder_2_out_0), .out_1(decoder_2_out_1), .out_2(decoder_2_out_2),
    .out_3(decoder_2_out_3), .out_4(decoder_2_out_4));  // open: out_5, out_6, out_7
  Multiplexer #(.Bits(16)) multiplexer_1 (
    .sel(decoder_2_out_0), .in_0(DP_Count), .in_1(_16bitfulladder_1_sum), .out(multiplexer_1_out));
  Multiplexer #(.Bits(16)) multiplexer_2 (
    .sel(decoder_2_out_1), .in_0(MEM_Count), .in_1(_16bitfulladder_1_sum), .out(multiplexer_2_out));
  Multiplexer #(.Bits(16)) multiplexer_3 (
    .sel(decoder_2_out_2), .in_0(Branch_Count), .in_1(_16bitfulladder_1_sum), .out(multiplexer_3_out));
  Multiplexer #(.Bits(16)) multiplexer_4 (
    .sel(decoder_2_out_3), .in_0(MUL_Count), .in_1(_16bitfulladder_1_sum), .out(multiplexer_4_out));
  Multiplexer #(.Bits(16)) multiplexer_5 (
    .sel(decoder_2_out_4), .in_0(BX_Count), .in_1(_16bitfulladder_1_sum), .out(multiplexer_5_out));
  _16BitRegister _16bitregister_1 (.D(multiplexer_1_out), .CLK(and_1_out), .CLR(CLR_out), .Q(DP_Count));
  _16BitRegister _16bitregister_2 (.D(multiplexer_2_out), .CLK(and_1_out), .CLR(CLR_out), .Q(MEM_Count));
  _16BitRegister _16bitregister_3 (.D(multiplexer_3_out), .CLK(and_1_out), .CLR(CLR_out), .Q(Branch_Count));
  _16BitRegister _16bitregister_4 (.D(multiplexer_4_out), .CLK(and_1_out), .CLR(CLR_out), .Q(MUL_Count));
  _16BitRegister _16bitregister_5 (.D(multiplexer_5_out), .CLK(and_1_out), .CLR(CLR_out), .Q(BX_Count));
  Multiplexer #(.Selector_Bits(3), .Bits(16)) multiplexer_6 (
    .sel(decoder_1_type), .in_0(DP_Count), .in_1(MEM_Count), .in_2(Branch_Count), .in_3(MUL_Count),
    .in_4(BX_Count), .in_5({16{1'b0}}), .in_6({16{1'b0}}), .in_7({16{1'b0}}), .out(multiplexer_6_out));
endmodule
