// Digital circuit TestAnalyzer.dig as structural Verilog
module TestAnalyzer (
  input  PN,
  input  CLR,
  input  CLK,
  output [15:0] out_1,
  output [15:0] out_2,
  output [15:0] out_3,
  output [15:0] out_4,
  output [15:0] out_5,
  output [15:0] out_6
);

  S_A s_a_1 (
    .PN(PN), .CLR(CLR), .CLK(CLK), .Inst_Count(out_1), .DP_Count(out_2), .MEM_Count(out_3),
    .Branch_Count(out_4), .MUL_Count(out_5), .BX_Count(out_6));

  // Notes on the sheet:
  //   CLR: default 1
endmodule
