// Digital circuit d-flipflop-clr.dig as structural Verilog
module d_flipflop_clr (
  input  D,
  input  CLK,
  input  CLR,
  output Q
);

  wire d_latch_clr_1_q, not_1_out;

  not not_1 (not_1_out, CLK);
  d_latch_clr d_latch_clr_1 (.CLK(not_1_out), .D(D), .CLR(CLR), .Q(d_latch_clr_1_q));  // open: nQ
  d_latch_clr d_latch_clr_2 (.CLK(CLK), .D(d_latch_clr_1_q), .CLR(CLR), .Q(Q));  // open: nQ
endmodule
