// Digital circuit d-latch-clr.dig as structural Verilog
module d_latch_clr (
  input  CLK,
  input  D,
  input  CLR,
  output Q,
  output nQ
);

  wire and_1_out, and_2_out, and_3_out, or_1_out;

  or or_1 (or_1_out, CLK, CLR);
  and and_1 (and_1_out, D, ~CLR);  // And
  and and_2 (and_2_out, or_1_out, ~and_1_out);  // And
  and and_3 (and_3_out, or_1_out, and_1_out);
  // sr_latch sr_latch_1: pin names not known; wires that end beside it: and_2_out, and_3_out, Q, nQ
endmodule
